// Digital circuit ALU.dig as structural Verilog
module ALU (
  input  [15:0] A,
  input  [15:0] B,
  input  [2:0] ALUFunc,
  output [15:0] ALUout,
  output Z,
  output N,
  output C,
  output V
);

  wire Add_c_o, and_2_out, and_3_out, comparator_1_eq, comparator_2_eq, comparator_3_eq, comparator_4_eq,
       Sub_c_o;
  wire [15:0] Add_s, and_1_out, or_1_out, SHL_out, SHR_out, Sub_s, xor_1_out;

  Add #(.Bits(16)) Add (.a(A), .b(B), .c_i(1'b0), .s(Add_s), .c_o(Add_c_o));
  Sub #(.Bits(16)) Sub (.a(A), .b(B), .c_i(1'b0), .s(Sub_s), .c_o(Sub_c_o));
  assign and_1_out = A & B;  // And and_1, 16 bits wide
  assign or_1_out = A | B;  // Or or_1, 16 bits wide
  assign xor_1_out = A ^ B;  // XOr xor_1, 16 bits wide
  BarrelShifter #(.Bits(16)) SHL (.in(A), .shift({1'b0, B[3:0]}), .out(SHL_out));
  BarrelShifter #(.Bits(16), .direction("right")) SHR (.in(A), .shift({1'b0, B[3:0]}), .out(SHR_out));
  Comparator comparator_1 (.a(A[15]), .b(B[15]), .eq(comparator_1_eq));  // open: gt, lt
  Comparator comparator_2 (.a(ALUout[15]), .b(A[15]), .eq(comparator_2_eq));  // open: gt, lt
  Comparator comparator_3 (.a(A[15]), .b(B[15]), .eq(comparator_3_eq));  // open: gt, lt
  Comparator comparator_4 (.a(ALUout[15]), .b(A[15]), .eq(comparator_4_eq));  // open: gt, lt
  Multiplexer #(.Selector_Bits(3), .Bits(16)) multiplexer_1 (
    .sel(ALUFunc), .in_0(Add_s), .in_1(Sub_s), .in_2(and_1_out), .in_3(or_1_out), .in_4(xor_1_out),
    .in_5(SHL_out), .in_6(SHR_out), .in_7(Add_s), .out(ALUout));
  Multiplexer #(.Selector_Bits(3)) multiplexer_2 (
    .sel(ALUFunc), .in_0(Add_c_o), .in_1(Sub_c_o), .in_2(1'b0), .in_3(1'b0), .in_4(1'b0), .in_5(1'b0),
    .in_6(1'b0), .in_7(1'b0), .out(C));
  and and_2 (and_2_out, comparator_1_eq, ~comparator_2_eq);  // And
  and and_3 (and_3_out, ~comparator_3_eq, ~comparator_4_eq);  // And
  Comparator #(.Bits(16)) comparator_5 (.a(ALUout), .b({16{1'b0}}), .eq(Z));  // open: gt, lt
  Multiplexer #(.Selector_Bits(3)) multiplexer_3 (
    .sel(ALUFunc), .in_0(and_2_out), .in_1(and_3_out), .in_2(1'b0), .in_3(1'b0), .in_4(1'b0), .in_5(1'b0),
    .in_6(1'b0), .in_7(1'b0), .out(V));

  assign N = ALUout[15];

  // Other names for the same wires on the sheet: aluf[2:0] = ALUFunc; Rd_15 = ALUout[15]
endmodule
