// Digital circuit CPU.dig as structural Verilog
module CPU (
  input  CLK,
  input  DBG_EN,
  input  [15:0] DBG_MADDR,
  input  RESET,
  input  [2:0] DBG_RSEL,
  output [15:0] DBG_MOUT,
  output [7:0] PC_OUT,
  output [3:0] FLAGS_OUT,
  output [15:0] DBG_ROUT,
  output [15:0] IR_OUT
);

  wire ALUSrcA, and_1_out, and_2_out, FlagWr, MemRd, MemWr, or_1_out, RegDst, RegW;
  wire [1:0] ALUSrcB, PCSrc, WBSel;
  wire [2:0] ALUFunc, RS1__ADDR, RS2__ADDR, WR__ADDR;
  wire [3:0] alu_1_z, multiplexer_10_out;
  wire [7:0] branch__target, multiplexer_1_out, multiplexer_2_out, PC__plusOne;
  wire [15:0] ALUout, imm4__ext, imm7__ext, multiplexer_5_out, multiplexer_6_out, multiplexer_9_out,
       offset10__ext, RS1__DATA, WR__DATA;

  Multiplexer #(.Selector_Bits(2), .Bits(8)) multiplexer_1 (
    .sel(PCSrc), .in_0(PC__plusOne), .in_1(branch__target), .in_2(RS1__DATA[7:0]), .in_3({8{1'b0}}),
    .out(multiplexer_1_out));
  Multiplexer #(.Bits(8)) multiplexer_2 (
    .sel(RESET), .in_0(multiplexer_1_out), .in_1({8{1'b0}}), .out(multiplexer_2_out));
  Register #(.Bits(8)) PC (.D(multiplexer_2_out), .C(CLK), .en(1'b1), .Q(PC_OUT));
  Add #(.Bits(8)) PC_plus_1 (.a(PC_OUT), .b(8'h1), .c_i(1'b0), .s(PC__plusOne));  // open: c_o
  Add #(.Bits(8)) add_1 (.a(PC__plusOne), .b(offset10__ext[7:0]), .c_i(1'b0), .s(branch__target));  // open: c_o
  ROM #(.AddrBits(8), .isProgramMemory("true"), .Bits(16)) IMEM (.A(PC_OUT), .sel(1'b1), .D(IR_OUT));
  ControlUnit controlunit_1 (
    .Z(FLAGS_OUT[0]), .N(FLAGS_OUT[1]), .V(FLAGS_OUT[3]), .CC(IR_OUT[15:14]), .S(IR_OUT[0]),
    .OPCODE(IR_OUT[13:10]), .RegW(RegW), .MemWr(MemWr), .MemRd(MemRd), .FlagWr__final(FlagWr),
    .RegDst(RegDst), .ALUSrcA(ALUSrcA), .ALUSrcB(ALUSrcB), .WBSel(WBSel), .ALUFunc(ALUFunc), .PCSrc(PCSrc));
  BitExtender #(.inputBits(4)) bitextender_1 (.in(IR_OUT[3:0]), .out(imm4__ext));
  BitExtender #(.inputBits(7)) bitextender_2 (.in(IR_OUT[6:0]), .out(imm7__ext));
  BitExtender #(.inputBits(10)) bitextender_3 (.in(IR_OUT[9:0]), .out(offset10__ext));
  RegisterFile registerfile_1 (
    .CLK(CLK), .RS1__ADDR(RS1__ADDR), .RS2__ADDR(RS2__ADDR), .WR__ADDR(WR__ADDR), .WR__DATA(WR__DATA),
    .REG__WRITE(RegW), .DBG__RSEL(DBG_RSEL), .DBG__EN(DBG_EN), .RS1__DATA(RS1__DATA), .RS2__DATA(DBG_ROUT));
  Multiplexer #(.Bits(3)) multiplexer_3 (.sel(RegDst), .in_0(IR_OUT[9:7]), .in_1(3'b111), .out(WR__ADDR));
  Multiplexer #(.Selector_Bits(2), .Bits(16)) multiplexer_4 (
    .sel(WBSel), .in_0(ALUout), .in_1(DBG_MOUT), .in_2({IR_OUT[6:0], {9{1'b0}}}),
    .in_3({{8{1'b0}}, PC__plusOne}), .out(WR__DATA));
  and and_1 (and_1_out, ~IR_OUT[10], IR_OUT[11], IR_OUT[12], IR_OUT[13]);  // And
  Multiplexer #(.Bits(16)) multiplexer_5 (.sel(ALUSrcA), .in_0(RS1__DATA), .in_1({16{1'b0}}), .out(multiplexer_5_out));
  Multiplexer #(.Selector_Bits(2), .Bits(16)) multiplexer_6 (
    .sel(ALUSrcB), .in_0(DBG_ROUT), .in_1(imm4__ext), .in_2(imm7__ext), .in_3({16{1'b0}}),
    .out(multiplexer_6_out));
  Multiplexer #(.Bits(3)) multiplexer_7 (.sel(MemWr), .in_0(IR_OUT[3:1]), .in_1(IR_OUT[9:7]), .out(RS2__ADDR));
  Multiplexer #(.Bits(3)) multiplexer_8 (.sel(and_1_out), .in_0(IR_OUT[6:4]), .in_1(IR_OUT[9:7]), .out(RS1__ADDR));
  ALU alu_1 (
    .A(multiplexer_5_out), .B(multiplexer_6_out), .ALUFunc(ALUFunc), .ALUout(ALUout), .Z(alu_1_z[0]),
    .N(alu_1_z[1]), .C(alu_1_z[2]), .V(alu_1_z[3]));
  Multiplexer #(.Bits(16)) multiplexer_9 (.sel(DBG_EN), .in_0(ALUout), .in_1(DBG_MADDR), .out(multiplexer_9_out));
  and and_2 (and_2_out, MemWr, ~DBG_EN);  // And
  Multiplexer #(.Bits(4)) multiplexer_10 (.sel(RESET), .in_0(alu_1_z), .in_1(4'b0000), .out(multiplexer_10_out));
  or or_1 (or_1_out, DBG_EN, MemRd);
  RAMDualPort #(.AddrBits(16), .Bits(16)) DMEM (
    .A(multiplexer_9_out), .Din(DBG_ROUT), .str(and_2_out), .C(CLK), .ld(or_1_out), .D(DBG_MOUT));
  Register #(.Bits(4)) register_1 (.D(multiplexer_10_out), .C(CLK), .en(FlagWr), .Q(FLAGS_OUT));

  // Other names for the same wires on the sheet: DBG__EN = DBG_EN; DBG__MADDR[15:0] = DBG_MADDR;
  //   DBG__RSEL[2:0] = DBG_RSEL; Dout[15:0] = DBG_MOUT; FLAGS__OUT[3:0] = FLAGS_OUT; imm7[6:0] = IR_OUT[6:0];
  //   IR__OUT[15:0] = IR_OUT; S = IR_OUT[0]; Rs2[2:0] = IR_OUT[3:1]; Rs1[2:0] = IR_OUT[6:4]; Rd[2:0] = IR_OUT[9:7];
  //   OPCODE[3:0] = IR_OUT[13:10]; CC[1:0] = IR_OUT[15:14]; PC__OUT[7:0] = PC_OUT; RS2__DATA[15:0] = DBG_ROUT

  // Notes on the sheet:
  //   IMEM loads prog.hex
endmodule
