// Digital circuit ControlUnit.dig as structural Verilog
module ControlUnit (
  input  Z,
  input  N,
  input  V,
  input  [1:0] CC,
  input  S,
  input  [3:0] OPCODE,
  output RegW,
  output MemWr,
  output MemRd,
  output FlagWr__final,
  output RegDst,
  output ALUSrcA,
  output [1:0] ALUSrcB,
  output [1:0] WBSel,
  output [2:0] ALUFunc,
  output [1:0] PCSrc
);

  wire cond__met, FlagCapable, MemWr__raw, RegW__raw;
  wire [1:0] PCSrc__raw;
  wire [12:12] rom_1_d;

  ROM #(.AddrBits(4), .Bits(13)) rom_1 (
    .A(OPCODE), .sel(1'b1),
    .D({rom_1_d[12], MemRd, FlagCapable, PCSrc__raw, WBSel, ALUSrcB, ALUSrcA, RegDst, MemWr__raw, RegW__raw}));
  Multiplexer #(.Selector_Bits(2)) multiplexer_1 (.sel(CC), .in_0(1'b1), .in_1(Z), .in_2(N), .in_3(V), .out(cond__met));
  and and_1 (RegW, RegW__raw, cond__met);
  and and_2 (MemWr, MemWr__raw, cond__met);
  and and_3 (FlagWr__final, FlagCapable, S, cond__met);
  Multiplexer #(.Bits(2)) multiplexer_2 (.sel(cond__met), .in_0(2'b00), .in_1(PCSrc__raw), .out(PCSrc));
  Multiplexer #(.Bits(3)) multiplexer_3 (.sel(rom_1_d[12]), .in_0(3'b000), .in_1(OPCODE[2:0]), .out(ALUFunc));

  // Notes on the sheet:
  //   contents of rom_1 (hex, n*v repeats v):
  //   7*1401,11,851,12,29,81,100,1c5,200
endmodule
