// Digital circuit RegisterFile.dig as structural Verilog
module RegisterFile (
  input  CLK,
  input  [2:0] RS1__ADDR,
  input  [2:0] RS2__ADDR,
  input  [2:0] WR__ADDR,
  input  [15:0] WR__DATA,
  input  REG__WRITE,
  input  [2:0] DBG__RSEL,
  input  DBG__EN,
  output [15:0] RS1__DATA,
  output [15:0] RS2__DATA
);

  wire and_1_out, RS1__ADDR__eq_0, RS2__ADDR__eq_0, WR__ADDR__eq_0;
  wire [2:0] multiplexer_1_out;
  wire [15:0] RegisterFile_da, RegisterFile_db;

  or or_1 (WR__ADDR__eq_0, WR__ADDR[0], WR__ADDR[1], WR__ADDR[2]);
  and and_1 (and_1_out, WR__ADDR__eq_0, REG__WRITE);
  Multiplexer #(.Bits(3)) multiplexer_1 (.sel(DBG__EN), .in_0(RS2__ADDR), .in_1(DBG__RSEL), .out(multiplexer_1_out));
  or or_2 (RS1__ADDR__eq_0, RS1__ADDR[0], RS1__ADDR[1], RS1__ADDR[2]);
  RegisterFile #(.AddrBits(3), .Bits(16)) RegisterFile (
    .Din(WR__DATA), .we(and_1_out), .Rw(WR__ADDR), .C(CLK), .Ra(RS1__ADDR), .Rb(multiplexer_1_out),
    .Da(RegisterFile_da), .Db(RegisterFile_db));
  Multiplexer #(.Bits(16)) multiplexer_2 (
    .sel(RS1__ADDR__eq_0), .in_0({16{1'b0}}), .in_1(RegisterFile_da), .out(RS1__DATA));
  Multiplexer #(.Bits(16)) multiplexer_3 (
    .sel(RS2__ADDR__eq_0), .in_0({16{1'b0}}), .in_1(RegisterFile_db), .out(RS2__DATA));
  or or_3 (RS2__ADDR__eq_0, RS2__ADDR[0], RS2__ADDR[1], RS2__ADDR[2]);

  // Other names for the same wires on the sheet: Rs1[2:0] = RS1__ADDR; Rs2[2:0] = RS2__ADDR
endmodule
